# Fritzing sketch saitek-pedal-controller (saved by Fritzing 0.9.3b)
circuit board: 8.46667cm x 5.64444cm
breadboards: 1

parts:
  Pro_Micro1 = SparkFun Pro Micro
  U2 = RJ45 Jack [package=rj45-8]
  S1 = Pushbutton [package="[SMD]"]
  R1 = Resistor [tolerance=±5% resistance=220 package=THT]
  LED1 = LED - 5mm [color="Red (633nm)" package="5 mm [THT]"]

nets:
  N1: Pro_Micro1.TX0, U2.2
  N2: Pro_Micro1.RX1, U2.4
  N3: Pro_Micro1.GND, U2.5, S1.Pin_3, S1.Pin_4, LED1.cathode
  N4: Pro_Micro1.2, U2.7
  N5: Pro_Micro1.3, U2.1
  N6: Pro_Micro1.5, S1.Pin_1, S1.Pin_2
  N7: Pro_Micro1.10, U2.8
  N8: Pro_Micro1.16, U2.3
  N9: Pro_Micro1.14, R1.Pin_1
  N10: Pro_Micro1.VCC, U2.6
  N11: R1.Pin_0, LED1.anode

custom parts:
  SparkFun Pro Micro: The Pro Micro is similar to the Pro Mini except with an ATmega32U4 on board. The USB transceiver inside the 32U4 allows us to add USB connectivity on-board and do away with bulky external USB interface. Based on: https://github.com/unorthodox-engineers/unorthodox-arduino/blob/master/Unorthodox/fritzing/parts/Pro%20Micro.fzpz
